// Digital circuit praktikum 5.1.dig as structural Verilog
module praktikum_5_1 (
  input  A,
  input  B,
  input  C
);

  wire and_1_out, and_2_out, not_1_out, or_1_out, or_2_out;

  not not_1 (not_1_out, B);
  or or_1 (or_1_out, A, C);
  and and_1 (and_1_out, not_1_out, C);
  and and_2 (and_2_out, or_1_out, and_1_out);
  or or_2 (or_2_out, A, and_2_out, B);
  LED X (.in(or_2_out));
endmodule
